// Logisim project Add_1.circ as structural Verilog: 2 circuits, main circuit main
module main (
  input  A,
  input  B,
  input  C,
  output V,
  output S
);

  Add_1 add_1_1 (.A(C), .B(A), .C(B), .V(V), .S(S));
endmodule

// S
module Add_1 (
  input  A,
  input  B,
  input  C,
  output V,
  output S
);

  wire and_1_out, and_2_out, or_1_out, xor_1_out;

  or or_1 (or_1_out, C, B);
  xor xor_1 (xor_1_out, A, B);
  and and_1 (and_1_out, or_1_out, A);
  and and_2 (and_2_out, B, C);
  xor xor_2 (S, xor_1_out, C);
  or or_2 (V, and_1_out, and_2_out);
endmodule
